// Logisim project Lab1.circ as structural Verilog
module LATCH_NOR (
  input  Set,
  input  Reset,
  output Q_inv,
  output Q
);

  nor nor_1 (Q_inv, Set, Q);
  nor nor_2 (Q, Q_inv, Reset);
endmodule

module LATCH_NAND (
  input  Set,
  input  Reset,
  output Q,
  output Q_inv
);

  nand nand_1 (Q, Set, Q_inv);
  nand nand_2 (Q_inv, Q, Reset);
endmodule

module LATCH_D (
  input  D,
  output Q,
  output Q_Inv
);

  wire not_1_out;

  not not_1 (not_1_out, D);
  nor nor_1 (Q, not_1_out, Q_Inv);
  nor nor_2 (Q_Inv, Q, D);
endmodule

module FF_SR_A (
  input  S,
  input  R,
  input  CLK,
  output Q,
  output Q_inv
);

  S_R_Flip_Flop s_r_ff_1 (.S(S), .R(R), .clk(CLK), .Q(Q), .Qn(Q_inv));  // open: reset, preset
endmodule

module FF_SR_B (
  input  S,
  input  R,
  input  CLK,
  output Q,
  output Q_inv
);

  S_R_Flip_Flop #(.trigger("falling")) s_r_ff_1 (.S(S), .R(R), .clk(CLK), .Q(Q), .Qn(Q_inv));  // open: reset, preset
endmodule

module FF_SR_C (
  input  D,
  input  CLK,
  output Q,
  output Q_inv
);

  wire not_1_out;

  not not_1 (not_1_out, D);
  S_R_Flip_Flop #(.trigger("falling")) s_r_ff_1 (
    .S(D), .R(not_1_out), .clk(CLK), .Q(Q), .Qn(Q_inv));  // open: reset, preset
endmodule

module FF_D (
  input  Dados,
  input  CLK,
  output Q1,
  output Q0,
  output Q2,
  output Q3
);

  D_Flip_Flop d_ff_1 (.D(Dados), .clk(CLK), .Q(Q3));  // open: Qn, preset, reset
  D_Flip_Flop d_ff_2 (.D(Q3), .clk(CLK), .Q(Q2));  // open: Qn, preset, reset
  D_Flip_Flop d_ff_3 (.D(Q2), .clk(CLK), .Q(Q1));  // open: Qn, preset, reset
  D_Flip_Flop d_ff_4 (.D(Q1), .clk(CLK), .Q(Q0));  // open: Qn, preset, reset
endmodule
