// Logisim project ELDI_Revisao.circ as structural Verilog: 14 circuits, main circuit main
module main (
);

  wire Cancelar_out, Chamar_out, cir6_1_q;

  Button Chamar (.out(Chamar_out));
  Button Cancelar (.out(Cancelar_out));
  CIR1 cir1_1 ();  // open: I0, I1, I2, I3, Sel, Saida
  CIR2 cir2_1 ();  // open: Entrada, Sel, O0, O1, O2, O3
  CIR3 cir3_1 ();  // open: ENTRADA, O0, O1, O2, O3, O4, O5, O6, O7
  CIR4 cir4_1 ();  // open: T0, T1, T2, T3, T4, T5, T6, T7, S
  CIR5 cir5_1 ();  // open: A, B, S
  LED led_1 (.in(cir6_1_q));
  CIR6 cir6_1 (.S(Chamar_out), .R(Cancelar_out), .Q(cir6_1_q));
endmodule

module CIR1 (
  input  I0,
  input  I1,
  input  I2,
  input  I3,
  input  [1:0] Sel,
  output Saida
);

  Multiplexer #(.select(2)) multiplexer_1 (.in0(I0), .in1(I1), .in2(I2), .in3(I3), .out(Saida), .sel(Sel));

  // Notes on the sheet:
  //   Multiplexador de 4 canais
endmodule

module CIR2 (
  input  Entrada,
  input  [1:0] Sel,
  output O0,
  output O1,
  output O2,
  output O3
);

  Demultiplexer #(.select(2)) demultiplexer_1 (.out0(O0), .out1(O1), .out2(O2), .out3(O3), .in(Entrada), .sel(Sel));

  // Notes on the sheet:
  //   Demultiplexador de 4 canais
endmodule

module CIR3 (
  input  [2:0] ENTRADA,
  output O0,
  output O1,
  output O2,
  output O3,
  output O4,
  output O5,
  output O6,
  output O7
);

  Decoder #(.enable("false"), .select(3)) decoder_1 (
    .out0(O0), .out1(O1), .out2(O2), .out3(O3), .out4(O4), .out5(O5), .out6(O6), .out7(O7), .sel(ENTRADA));
endmodule

module CIR4 (
  input  T0,
  input  T1,
  input  T2,
  input  T3,
  input  T4,
  input  T5,
  input  T6,
  input  T7,
  output [2:0] S
);

  Priority_Encoder priority_encoder_1 (
    .in0(T0), .in1(T1), .in2(T2), .in3(T3), .in4(T4), .in5(T5), .in6(T6), .in7(T7), .out(S));  // open: en_in, gs, en_out
endmodule

module CIR5 (
  input  [3:0] A,
  input  [3:0] B,
  output [3:0] S
);

  _74283 #(.ShowInternalStructure("true")) u_74283_1 (
    .pin1(S[1]), .pin2(B[1]), .pin3(A[1]), .pin4(S[0]), .pin5(A[0]), .pin6(B[0]), .pin15(B[2]), .pin14(A[2]),
    .pin13(S[2]), .pin12(A[3]), .pin11(B[3]), .pin10(S[3]));  // open: pin7, pin9
endmodule

module CIR6 (
  input  S,
  input  R,
  output Q
);

  wire nand_2_out;

  nand nand_1 (Q, ~S, nand_2_out);  // NAND_Gate
  nand nand_2 (nand_2_out, Q, ~R);  // NAND_Gate
endmodule

module Caixa_Banco (
  input  CX1,
  input  CX2,
  input  CX3,
  input  CX4,
  input  CX5,
  input  CX6,
  output Sa,
  output Sb,
  output Sc,
  output Sd,
  output Se,
  output Sf,
  output Sg
);

  wire and_6_out, not_1_out, not_3_out, not_4_out, not_5_out, not_6_out;

  not not_1 (not_1_out, CX1);
  not not_2 (Sc, CX2);
  not not_3 (not_3_out, CX3);
  not not_4 (not_4_out, CX4);
  not not_5 (not_5_out, CX5);
  not not_6 (not_6_out, CX6);
  and and_1 (Sa, not_1_out, not_4_out);
  and and_2 (Sb, not_5_out, not_6_out);
  and and_3 (Sd, not_1_out, not_4_out);
  and and_4 (Se, not_1_out, not_3_out, not_4_out, not_5_out);
  and and_5 (Sf, not_1_out, Sc, not_3_out);
  and and_6 (and_6_out, not_1_out, CX4);
  or or_1 (Sg, CX6, CX5, and_6_out, CX3, CX2);
endmodule

module Projeto1 (
);

  wire a, b, c, caixa1_out, caixa2_out, caixa3_out, caixa4_out, caixa5_out, caixa6_out, d, e, f, g;

  Button caixa1 (.out(caixa1_out));
  Button caixa2 (.out(caixa2_out));
  Button caixa3 (.out(caixa3_out));
  Button caixa4 (.out(caixa4_out));
  Button caixa5 (.out(caixa5_out));
  Button caixa6 (.out(caixa6_out));
  Caixa_Banco caixa_banco_1 (
    .CX1(caixa1_out), .CX2(caixa2_out), .CX3(caixa3_out), .CX4(caixa4_out), .CX5(caixa5_out),
    .CX6(caixa6_out), .Sa(a), .Sb(b), .Sc(c), .Sd(d), .Se(e), .Sf(f), .Sg(g));
  _7_Segment_Display u_7_segment_display_1 (.g(g), .f(f), .a(a), .b(b), .e(e), .d(d), .c(c));  // open: dp
endmodule

module memoria (
  input  [6:0] ENTRADA,
  input  CLK,
  output [6:0] SAIDA
);

  Register #(.trigger("falling"), .width(7)) register_1 (.D(ENTRADA), .clk(CLK), .Q(SAIDA));  // open: en, clr
endmodule

module Projeto2 (
);

  wire a, b, c, caixa1_out, caixa2_out, caixa3_out, caixa4_out, caixa5_out, caixa6_out, d, e, f, g, or_1_out;
  wire [6:0] caixa_banco_1_sa;

  Button caixa1 (.out(caixa1_out));
  Button caixa2 (.out(caixa2_out));
  Button caixa3 (.out(caixa3_out));
  Button caixa4 (.out(caixa4_out));
  Button caixa5 (.out(caixa5_out));
  Button caixa6 (.out(caixa6_out));
  or or_1 (or_1_out, caixa1_out, caixa2_out, caixa3_out, caixa4_out, caixa5_out, caixa6_out);
  Caixa_Banco caixa_banco_1 (
    .CX1(caixa1_out), .CX2(caixa2_out), .CX3(caixa3_out), .CX4(caixa4_out), .CX5(caixa5_out),
    .CX6(caixa6_out), .Sa(caixa_banco_1_sa[0]), .Sb(caixa_banco_1_sa[1]), .Sc(caixa_banco_1_sa[2]),
    .Sd(caixa_banco_1_sa[3]), .Se(caixa_banco_1_sa[4]), .Sf(caixa_banco_1_sa[5]), .Sg(caixa_banco_1_sa[6]));
  memoria memoria_1 (.ENTRADA(caixa_banco_1_sa), .CLK(or_1_out), .SAIDA({g, f, e, d, c, b, a}));
  _7_Segment_Display u_7_segment_display_1 (.g(g), .f(f), .a(a), .b(b), .e(e), .d(d), .c(c));  // open: dp
endmodule

module MUX_Portas_logicas (
  input  I0,
  input  I1,
  input  I2,
  input  I3,
  input  A_MSB,
  input  B_LSM,
  output S
);

  wire and_1_out, and_2_out, and_3_out, and_4_out;

  and and_1 (and_1_out, ~A_MSB, ~B_LSM, I0);  // AND_Gate
  and and_2 (and_2_out, ~A_MSB, B_LSM, I1);  // AND_Gate
  and and_3 (and_3_out, A_MSB, ~B_LSM, I2);  // AND_Gate
  and and_4 (and_4_out, A_MSB, B_LSM, I3);
  or or_1 (S, and_1_out, and_2_out, and_3_out, and_4_out);

  // Notes on the sheet:
  //   MSB - Bit mais significativo
  //   Multiplexador 4 canais
endmodule

module Demux_Portas_logicas (
  input  Entrada,
  input  A_MSB,
  input  B_LSM,
  output O0,
  output O1,
  output O2,
  output O3
);

  and and_1 (O0, ~A_MSB, ~B_LSM, Entrada);  // AND_Gate
  and and_2 (O1, ~A_MSB, B_LSM, Entrada);  // AND_Gate
  and and_3 (O2, A_MSB, ~B_LSM, Entrada);  // AND_Gate
  and and_4 (O3, A_MSB, B_LSM, Entrada);

  // Notes on the sheet:
  //   Demultiplexador 4 canais
endmodule

module MUx_Demux (
  input  in_1,
  input  in_2,
  input  in_3,
  input  in_4,
  input  [1:0] Chave_selecao,
  output out_6,
  output out_7,
  output out_8,
  output out_9
);

  wire mux_portas_logicas_1_s;

  MUX_Portas_logicas mux_portas_logicas_1 (
    .I0(in_1), .I1(in_2), .I2(in_3), .I3(in_4), .A_MSB(Chave_selecao[1]), .B_LSM(Chave_selecao[0]),
    .S(mux_portas_logicas_1_s));
  Demux_Portas_logicas demux_portas_logicas_1 (
    .Entrada(mux_portas_logicas_1_s), .A_MSB(Chave_selecao[1]), .B_LSM(Chave_selecao[0]), .O0(out_6),
    .O1(out_7), .O2(out_8), .O3(out_9));
endmodule
