// Logisim project Contadores_Juno.circ as structural Verilog: 7 circuits, main circuit main
module main (
  input  CLR
);

  wire clock_1_out, countmod60_1_rc1, countmod60_2_rc1;
  wire [3:0] countmod24_1_out_3, countmod24_1_out_4, countmod60_1_dezenas, countmod60_1_unidades,
       countmod60_2_dezenas, countmod60_2_unidades;

  CountMod24 countmod24_1 (.RC1(countmod60_1_rc1), .in_2(CLR), .out_3(countmod24_1_out_3), .out_4(countmod24_1_out_4));
  Hex_Digit_Display hex_digit_display_1 (.value(countmod24_1_out_4));  // open: dp
  Hex_Digit_Display hex_digit_display_2 (.value(countmod24_1_out_3));  // open: dp
  Hex_Digit_Display hex_digit_display_3 (.value(countmod60_1_dezenas));  // open: dp
  Hex_Digit_Display hex_digit_display_4 (.value(countmod60_1_unidades));  // open: dp
  Hex_Digit_Display hex_digit_display_5 (.value(countmod60_2_dezenas));  // open: dp
  CountMod60 countmod60_1 (
    .CLK(countmod60_2_rc1), .CLR(CLR), .Dezenas(countmod60_1_dezenas), .Unidades(countmod60_1_unidades),
    .RC1(countmod60_1_rc1));
  Hex_Digit_Display hex_digit_display_6 (.value(countmod60_2_unidades));  // open: dp
  Clock clock_1 (.out(clock_1_out));
  CountMod60 countmod60_2 (
    .CLK(clock_1_out), .CLR(CLR), .Dezenas(countmod60_2_dezenas), .Unidades(countmod60_2_unidades),
    .RC1(countmod60_2_rc1));
endmodule

module CountMod10 (
  input  CLK,
  input  CLR,
  output [3:0] saida,
  output RC0
);

  wire or_1_out;

  T_Flip_Flop #(.trigger("falling")) t_ff_1 (.T(1'b1), .clk(CLK), .Q(saida[0]), .reset(or_1_out));  // open: Qn, preset
  or or_1 (or_1_out, RC0, CLR);
  T_Flip_Flop #(.trigger("falling")) t_ff_2 (
    .T(1'b1), .clk(saida[0]), .Q(saida[1]), .reset(or_1_out));  // open: Qn, preset
  T_Flip_Flop #(.trigger("falling")) t_ff_3 (
    .T(1'b1), .clk(saida[1]), .Q(saida[2]), .reset(or_1_out));  // open: Qn, preset
  and DEC10 (RC0, saida[1], saida[3]);
  T_Flip_Flop #(.trigger("falling")) t_ff_4 (
    .T(1'b1), .clk(saida[2]), .Q(saida[3]), .reset(or_1_out));  // open: Qn, preset

  // Other names for the same wires on the sheet: M10[3:0] = saida; Q0 = saida[0]; Q1 = saida[1]; Q2 = saida[2];
  //   Q3 = saida[3]
endmodule

module CountMod100 (
  input  in_1
);

  wire RC0;
  wire [3:0] countmod10_1_saida, countmod10_2_saida;

  Hex_Digit_Display hex_digit_display_1 (.value(countmod10_1_saida));  // open: dp
  CountMod10 countmod10_1 (.CLK(in_1), .CLR(in_1), .saida(countmod10_1_saida));  // open: RC0
  Hex_Digit_Display hex_digit_display_2 (.value(countmod10_2_saida));  // open: dp
  CountMod10 countmod10_2 (.CLK(in_1), .CLR(in_1), .saida(countmod10_2_saida), .RC0(RC0));
endmodule

module CountMod6 (
  input  CLK,
  input  CLR,
  output [3:0] saida,
  output RC1
);

  wire or_1_out;

  T_Flip_Flop #(.trigger("falling")) t_ff_1 (.T(1'b1), .clk(CLK), .Q(saida[0]), .reset(or_1_out));  // open: Qn, preset
  or or_1 (or_1_out, RC1, CLR);
  T_Flip_Flop #(.trigger("falling")) t_ff_2 (
    .T(1'b1), .clk(saida[0]), .Q(saida[1]), .reset(or_1_out));  // open: Qn, preset
  T_Flip_Flop #(.trigger("falling")) t_ff_3 (
    .T(1'b1), .clk(saida[1]), .Q(saida[2]), .reset(or_1_out));  // open: Qn, preset
  and DEC10 (RC1, saida[1], saida[2]);

  assign saida[3] = 1'b0;

  // Other names for the same wires on the sheet: Q0 = saida[0]; Q1 = saida[1]; Q2 = saida[2]
endmodule

module CountMod60 (
  input  CLK,
  input  CLR,
  output [3:0] Dezenas,
  output [3:0] Unidades,
  output RC1
);

  wire RC0;

  Hex_Digit_Display hex_digit_display_1 (.value(Dezenas));  // open: dp
  CountMod6 CM6 (.CLK(RC0), .CLR(CLR), .saida(Dezenas), .RC1(RC1));
  Hex_Digit_Display hex_digit_display_2 (.value(Unidades));  // open: dp
  CountMod10 CM10 (.CLK(CLK), .CLR(CLR), .saida(Unidades), .RC0(RC0));
endmodule

module CountMod4 (
  input  CLK,
  input  CLR,
  output [3:0] saida
);

  wire and_1_out, or_1_out;

  T_Flip_Flop #(.trigger("falling")) t_ff_1 (.T(1'b1), .clk(CLK), .Q(saida[0]), .reset(or_1_out));  // open: Qn, preset
  or or_1 (or_1_out, and_1_out, CLR);
  T_Flip_Flop #(.trigger("falling")) t_ff_2 (
    .T(1'b1), .clk(saida[0]), .Q(saida[1]), .reset(or_1_out));  // open: Qn, preset
  and and_1 (and_1_out, saida[0], saida[1]);

  assign saida[3:2] = 2'b00;

  // Other names for the same wires on the sheet: Q0 = saida[0]; Q1 = saida[1]
endmodule

module CountMod24 (
  input  RC1,
  input  in_2,
  output [3:0] out_3,
  output [3:0] out_4
);

  wire and_1_out, countmod10_1_rc0, or_1_out;

  or or_1 (or_1_out, and_1_out, in_2);
  and and_1 (and_1_out, out_4[1], out_3[2]);
  CountMod10 countmod10_1 (.CLK(RC1), .CLR(or_1_out), .saida(out_3), .RC0(countmod10_1_rc0));
  CountMod4 countmod4_1 (.CLK(countmod10_1_rc0), .CLR(or_1_out), .saida(out_4));
  Hex_Digit_Display hex_digit_display_1 (.value(out_3));  // open: dp
  Hex_Digit_Display hex_digit_display_2 (.value(out_4));  // open: dp

  // Other names for the same wires on the sheet: CLR = in_2
endmodule
